# Fritzing sketch PA_0021 (saved by Fritzing 0.9.9b)
circuit board: 10.4035cm x 2.42361cm
breadboards: 1

parts:
  Bauteil6 = Arduino Nano (Rev3.0) (ICSP)
  F1E-Servo = Dagu DGServo 9g header (male) [package=THT]
  S2 = SWITCH-MOMENTARY-2 [package=tactile-pth]
  RD = TRIMPOT [package=trimpot_tc33]
  DT_Servo = Dagu DGServo 9g header (male) [package=THT]
  Sensor = 9-DOF Absolute Orientation IMU Fusion Breakout - BNO055
  R-P = TRIMPOT [package=trimpot_tc33]
  RI = TRIMPOT [package=trimpot_tc33]
  DT-Input = female pin header, 2 pins [form="♀ (female)"]
  R_Trim = TRIMPOT [package=trimpot_tc33]
  Power_5_V = female pin header, 2 pins [form="♀ (female)"]

nets:
  GND: Bauteil6.GND, F1E-Servo.gnd, S2.2, RD.CW, DT_Servo.gnd, Sensor.GND, R-P.CW, RI.CW, DT-Input.pin2, R_Trim.CW, Power_5_V.pin1
  N1: Bauteil6.D7, DT-Input.pin1
  N2: Bauteil6.D8, S2.1
  N3: Bauteil6.D9, F1E-Servo.pulse
  N4: Bauteil6.D10, DT_Servo.pulse
  VCC: Bauteil6.5V, F1E-Servo.Vcc, RD.CCW, DT_Servo.Vcc, Sensor.5.0V, R-P.CCW, RI.CCW, R_Trim.CCW, Power_5_V.pin2
  N5: Bauteil6.A5, Sensor.SCL_5V
  N6: Bauteil6.A4, Sensor.SDA_5V
  N7: Bauteil6.A3, RD.WIPER
  N8: Bauteil6.A2, RI.WIPER
  N9: Bauteil6.A1, R-P.WIPER
  N10: Bauteil6.A0, R_Trim.WIPER

custom parts:
  9-DOF Absolute Orientation IMU Fusion Breakout - BNO055: A MEMS accelerometer, magnetometer and gyroscope on a single die with a high speed ARM Cortex-M0 based processor to digest all the sensor data, abstract the sensor fusion and real time requirements away, and spit out data you can use in quaternions, Euler angles or vectors.
