# Fritzing sketch PA_0021_Seeduino (saved by Fritzing 0.9.9b)
circuit board: 8.26962cm x 2.36671cm
breadboards: 1

parts:
  F1E-Servo = Dagu DGServo 9g header (male) [package=THT]
  S2 = SWITCH-MOMENTARY-2 [package=tactile-pth]
  DT_Servo = Dagu DGServo 9g header (male) [package=THT]
  Seeduino = seeeduino-xiao
  J1 = female pin header, 2 pins [form="♀ (female)"]
  J2 = female pin header, 2 pins [form="♀ (female)"]
  Bauteil5 = 9-DOF Absolute Orientation IMU Fusion Breakout - BNO055
  RD = TRIMPOT [package=trimpot_tc33]
  RI = TRIMPOT [package=trimpot_tc33]
  R-P = TRIMPOT [package=trimpot_tc33]
  R_Trim = TRIMPOT [package=trimpot_tc33]

nets:
  GND: F1E-Servo.gnd, S2.2, DT_Servo.gnd, Seeduino.GND, J1.pin2, J2.pin1, Bauteil5.GND, RD.CW, RI.CW, R-P.CW, R_Trim.CW
  VCC: F1E-Servo.Vcc, DT_Servo.Vcc, Seeduino.5V, J2.pin2, Bauteil5.5.0V, RD.CCW, RI.CCW, R-P.CCW, R_Trim.CCW
  N1: F1E-Servo.pulse, Seeduino.D9
  N2: S2.1, Seeduino.D8
  N3: DT_Servo.pulse, Seeduino.D10
  N4: Seeduino.D0, R_Trim.WIPER
  N5: Seeduino.D1, R-P.WIPER
  N6: Seeduino.D2, RI.WIPER
  N7: Seeduino.D3, RD.WIPER
  N8: Seeduino.D4, Bauteil5.SDA_5V
  N9: Seeduino.D5, Bauteil5.SCL_5V
  N10: Seeduino.D7, J1.pin1

custom parts:
  seeeduino-xiao: Seeeduino XIAO processor board.
  9-DOF Absolute Orientation IMU Fusion Breakout - BNO055: A MEMS accelerometer, magnetometer and gyroscope on a single die with a high speed ARM Cortex-M0 based processor to digest all the sensor data, abstract the sensor fusion and real time requirements away, and spit out data you can use in quaternions, Euler angles or vectors.
