# Fritzing sketch PA_0022a_Seeduino2 (saved by Fritzing 0.9.9b)
circuit board: 10.0971cm x 2.76408cm
breadboards: 2

parts:
  R-P1 = TRIMPOT [package=trimpot_tc33]
  S2 = Toggle Switch [package=THT]
  C3 = Capacitor Polarized [package=panasonic_d]
  R_Trim1 = TRIMPOT [package=trimpot_tc33]
  IC3 = Voltage Regulator [part_number=MCP1700 package=SOT-89]
  RD1 = TRIMPOT [package=trimpot_tc33]
  Taster1 = SWITCH-MOMENTARY-2 [package=tactile-pth]
  F1E-Servo1 = Dagu DGServo 9g header (male) [package=THT]
  RI1 = TRIMPOT [package=trimpot_tc33]
  Vin1 = female pin header, 2 pins [form="♀ (female)"]
  Seeduino1 = seeeduino-xiao
  J2_-_DT1 = female pin header, 2 pins [form="♀ (female)"]
  DT_Servo1 = Dagu DGServo 9g header (male) [package=THT]
  Bauteil6 = 9-DOF Absolute Orientation IMU Fusion Breakout - BNO055
  J1_Reverse1 = female pin header, 2 pins [form="♀ (female)"]
  C4 = Capacitor Polarized [package=panasonic_d]

nets:
  VCC: R-P1.CCW, C3.+, R_Trim1.CCW, IC3.OUT, RD1.CCW, F1E-Servo1.Vcc, RI1.CCW, Seeduino1.5V, DT_Servo1.Vcc, Bauteil6.5.0V
  N1: R-P1.WIPER, Seeduino1.D1
  GND: R-P1.CW, C3.-, R_Trim1.CW, IC3.GND, RD1.CW, Taster1.2, F1E-Servo1.gnd, RI1.CW, Vin1.pin1, Seeduino1.GND, J2_-_DT1.pin2, DT_Servo1.gnd, Bauteil6.GND, J1_Reverse1.pin2, C4.-
  N2: S2.COM, Vin1.pin2
  N3: S2.L2, IC3.IN, C4.+
  N4: R_Trim1.WIPER, Seeduino1.D0
  N5: RD1.WIPER, Seeduino1.D3
  N6: Taster1.1, Seeduino1.D8
  N7: F1E-Servo1.pulse, Seeduino1.D9
  N8: RI1.WIPER, Seeduino1.D2
  N9: Seeduino1.D4, Bauteil6.SDA_5V
  N10: Seeduino1.D5, Bauteil6.SCL_5V
  N11: Seeduino1.D6, J1_Reverse1.pin1
  N12: Seeduino1.D7, J2_-_DT1.pin1
  N13: Seeduino1.D10, DT_Servo1.pulse

custom parts:
  Voltage Regulator: Voltage Regulator MCP1700
  seeeduino-xiao: Seeeduino XIAO processor board.
  9-DOF Absolute Orientation IMU Fusion Breakout - BNO055: A MEMS accelerometer, magnetometer and gyroscope on a single die with a high speed ARM Cortex-M0 based processor to digest all the sensor data, abstract the sensor fusion and real time requirements away, and spit out data you can use in quaternions, Euler angles or vectors.
